// Logisim project CPU (6).circ as structural Verilog: 1 circuit, main circuit main
module main (
  output [7:0] RegData1,
  output [7:0] RegData2
);

  wire and_1_out, and_2_out, and_3_out, and_4_out, clock_1_out, clock_2_out, decoder_1_out0, decoder_1_out1,
       decoder_1_out2, decoder_1_out3;
  wire [3:0] X0_q, X0_q_2, X1_q, X1_q_2, X2_q, X2_q_2, X3_q, X3_q_2;
  wire [7:0] adder_1_out, adder_2_out, DataMem_dout, InstructionMem_dout, multiplexer_1_out, register_1_q,
       subtractor_1_out;

  Clock #(.highDuration(2), .lowDuration(2)) clock_1 (.out(clock_1_out));
  Adder adder_1 (.a(RegData1), .b(RegData2), .out(adder_1_out));  // open: cin, cout
  Subtractor subtractor_1 (.a(RegData1), .b(RegData2), .out(subtractor_1_out));  // open: bin, bout
  Multiplexer #(.select(2), .width(8)) multiplexer_1 (
    .in0(DataMem_dout), .in1(adder_1_out), .in2(subtractor_1_out), .out(multiplexer_1_out),
    .sel(InstructionMem_dout[7:6]));  // open: in3
  Register register_1 (.D(adder_2_out), .en(1'b1), .clk(clock_1_out), .Q(register_1_q));  // open: clr
  Adder adder_2 (.a(register_1_q), .b(8'h1), .out(adder_2_out));  // open: cin, cout
  Clock clock_2 (.out(clock_2_out));
  RAM InstructionMem (
    .addr(register_1_q), .we(1'b0), .oe(1'b1), .clk(clock_1_out), .dout(InstructionMem_dout));  // open: din
  Decoder #(.select(2)) decoder_1 (
    .out0(decoder_1_out0), .out1(decoder_1_out1), .out2(decoder_1_out2), .out3(decoder_1_out3),
    .sel(InstructionMem_dout[1:0]), .en(1'b1));
  RAM #(.addrWidth(4)) DataMem (
    .addr(InstructionMem_dout[5:2]), .we(1'b0), .oe(1'b1), .clk(clock_2_out), .dout(DataMem_dout));  // open: din
  Register X0 (.D(multiplexer_1_out), .en(and_1_out), .clk(clock_1_out), .Q({X0_q_2, X0_q}));  // open: clr
  and and_1 (and_1_out, 1'b1, decoder_1_out0);
  Register X1 (.D(multiplexer_1_out), .en(and_2_out), .clk(clock_1_out), .Q({X1_q_2, X1_q}));  // open: clr
  and and_2 (and_2_out, 1'b1, decoder_1_out1);
  Register X2 (.D(multiplexer_1_out), .en(and_3_out), .clk(clock_1_out), .Q({X2_q_2, X2_q}));  // open: clr
  and and_3 (and_3_out, 1'b1, decoder_1_out2);
  Register X3 (.D(multiplexer_1_out), .en(and_4_out), .clk(clock_1_out), .Q({X3_q_2, X3_q}));  // open: clr
  and and_4 (and_4_out, 1'b1, decoder_1_out3);
  Hex_Digit_Display hex_digit_display_1 (.value(X0_q_2));  // open: dp
  Hex_Digit_Display hex_digit_display_2 (.value(X0_q));  // open: dp
  Hex_Digit_Display hex_digit_display_3 (.value(X1_q_2));  // open: dp
  Hex_Digit_Display hex_digit_display_4 (.value(X1_q));  // open: dp
  Hex_Digit_Display hex_digit_display_5 (.value(X2_q_2));  // open: dp
  Multiplexer #(.select(2), .width(8)) multiplexer_2 (
    .in0({X0_q_2, X0_q}), .in1({X1_q_2, X1_q}), .in2({X2_q_2, X2_q}), .in3({X3_q_2, X3_q}), .out(RegData1),
    .sel(InstructionMem_dout[5:4]));
  Multiplexer #(.select(2), .width(8)) multiplexer_3 (
    .in0({X0_q_2, X0_q}), .in1({X1_q_2, X1_q}), .in2({X2_q_2, X2_q}), .in3({X3_q_2, X3_q}), .out(RegData2),
    .sel(InstructionMem_dout[3:2]));
  Hex_Digit_Display hex_digit_display_6 (.value(X2_q));  // open: dp
  Hex_Digit_Display hex_digit_display_7 (.value(X3_q_2));  // open: dp
  Hex_Digit_Display hex_digit_display_8 (.value(X3_q));  // open: dp

  // Notes on the sheet:
  //   Max Takacs & Jacob Gurevich
  //   RegData1
  //   I pledge my honor that I have abided by the Stevens Honor System.
  //   RegData2
  //   RegWrite
  //   WriteReg
  //   RegDataW
  //   WriteReg
  //   Register File
  //   Data Memory
  //   Instruction Memory
  //   X0
  //   X1
  //   00 00 00 00
  //   X2
  //   ReadReg1
  //   ReadReg2
  //   X3
endmodule
